// Logisim project g1.circ as structural Verilog: 7 circuits, main circuit 1-bit sum
module _1_bit_sum (
  input  cin,
  input  a,
  input  b,
  output out_4
);

  wire and_1_out, and_2_out, and_3_out, and_4_out;

  and and_1 (and_1_out, ~cin, a, ~b);  // AND_Gate
  and and_2 (and_2_out, ~cin, ~a, b);  // AND_Gate
  and and_3 (and_3_out, cin, ~a, ~b);  // AND_Gate
  and and_4 (and_4_out, cin, a, b);
  or or_1 (out_4, and_1_out, and_2_out, and_3_out, and_4_out);
endmodule

module _1_bit_carryout (
  input  cin,
  input  a,
  input  b,
  output out_4
);

  wire and_1_out, and_2_out, and_3_out;

  and and_1 (and_1_out, cin, a);
  and and_2 (and_2_out, cin, b);
  and and_3 (and_3_out, a, b);
  or or_1 (out_4, and_1_out, and_2_out, and_3_out);
endmodule

module _1_bit_full_adder (
  input  cin,
  input  a,
  input  b,
  output sum,
  output cout
);

  _1_bit_sum u_1_bit_sum_1 (.cin(cin), .a(a), .b(b), .out_4(sum));
  _1_bit_carryout u_1_bit_carryout_1 (.cin(cin), .a(a), .b(b), .out_4(cout));
endmodule

module _1_bit_ALU (
  input  ainvert,
  input  binvert,
  input  cin,
  input  [1:0] op,
  input  a,
  input  b,
  input  less,
  output result,
  output cout
);

  wire and_1_out, multiplexer_1_out, multiplexer_2_out, n1_bit_full_adder_1_sum, not_1_out, not_2_out,
       or_1_out;

  Multiplexer multiplexer_1 (.in0(a), .in1(not_1_out), .out(multiplexer_1_out), .sel(ainvert));
  not not_1 (not_1_out, a);
  not not_2 (not_2_out, b);
  Multiplexer multiplexer_2 (.in0(b), .in1(not_2_out), .out(multiplexer_2_out), .sel(binvert));
  and and_1 (and_1_out, multiplexer_1_out, multiplexer_2_out);
  or or_1 (or_1_out, multiplexer_1_out, multiplexer_2_out);
  _1_bit_full_adder u_1_bit_full_adder_1 (
    .a(multiplexer_1_out), .b(multiplexer_2_out), .cin(cin), .cout(cout), .sum(n1_bit_full_adder_1_sum));
  Multiplexer #(.select(2)) multiplexer_3 (
    .in0(and_1_out), .in1(or_1_out), .in2(n1_bit_full_adder_1_sum), .in3(less), .out(result), .sel(op));
endmodule

module _4_bit_ALU (
  input  [3:0] Control,
  input  zero,
  input  [3:0] a,
  input  [3:0] b,
  output [3:0] result,
  output Zero_2,
  output Overflow
);

  wire n1_bit_alu_1_cout, n1_bit_alu_2_cout, n1_bit_alu_3_cout, n1_bit_full_adder_overflow_detect_1_set,
       or_1_out;

  _1_bit_ALU u_1_bit_alu_1 (
    .a(a[0]), .b(b[0]), .less(n1_bit_full_adder_overflow_detect_1_set), .ainvert(Control[3]),
    .binvert(Control[2]), .cin(Control[2]), .op(Control[1:0]), .cout(n1_bit_alu_1_cout), .result(result[0]));
  _1_bit_ALU u_1_bit_alu_2 (
    .a(a[1]), .b(b[1]), .less(zero), .ainvert(Control[3]), .binvert(Control[2]), .cin(n1_bit_alu_1_cout),
    .op(Control[1:0]), .cout(n1_bit_alu_2_cout), .result(result[1]));
  _1_bit_ALU u_1_bit_alu_3 (
    .a(a[2]), .b(b[2]), .less(zero), .ainvert(Control[3]), .binvert(Control[2]), .cin(n1_bit_alu_2_cout),
    .op(Control[1:0]), .cout(n1_bit_alu_3_cout), .result(result[2]));
  _1_bit_full_adder_overflow_detect u_1_bit_full_adder_overflow_detect_1 (
    .a(a[3]), .b(b[3]), .less(zero), .ainvert(Control[3]), .binvert(Control[2]), .cin(n1_bit_alu_3_cout),
    .op(Control[1:0]), .result(result[3]), .set(n1_bit_full_adder_overflow_detect_1_set), .Overflow(Overflow));
  not not_1 (Zero_2, or_1_out);
  or or_1 (or_1_out, result[0], result[1], result[2], result[3]);
endmodule

module _1_bit_full_adder_overflow_detect (
  input  ainvert,
  input  binvert,
  input  cin,
  input  [1:0] op,
  input  a,
  input  b,
  input  less,
  output result,
  output set,
  output Overflow
);

  wire and_1_out, multiplexer_1_out, multiplexer_2_out, n1_bit_full_adder_1_cout, not_1_out, not_2_out,
       or_1_out;

  Multiplexer multiplexer_1 (.in0(a), .in1(not_1_out), .out(multiplexer_1_out), .sel(ainvert));
  not not_1 (not_1_out, a);
  not not_2 (not_2_out, b);
  Multiplexer multiplexer_2 (.in0(b), .in1(not_2_out), .out(multiplexer_2_out), .sel(binvert));
  and and_1 (and_1_out, multiplexer_1_out, multiplexer_2_out);
  or or_1 (or_1_out, multiplexer_1_out, multiplexer_2_out);
  _1_bit_full_adder u_1_bit_full_adder_1 (
    .a(multiplexer_1_out), .b(multiplexer_2_out), .cin(cin), .cout(n1_bit_full_adder_1_cout), .sum(set));
  Overflow_detection overflow_detection_1 (.cin(cin), .cout(n1_bit_full_adder_1_cout), .Overflow(Overflow));
  Multiplexer #(.select(2)) multiplexer_3 (
    .in0(and_1_out), .in1(or_1_out), .in2(set), .in3(less), .out(result), .sel(op));
endmodule

module Overflow_detection (
  input  cin,
  input  cout,
  output Overflow
);

  wire and_1_out, and_2_out;

  and and_1 (and_1_out, ~cin, cout);  // AND_Gate
  and and_2 (and_2_out, cin, ~cout);  // AND_Gate
  or or_1 (Overflow, and_1_out, and_2_out);
endmodule
